# Fritzing sketch UCAAT2015Demo (saved by Fritzing 0.9.2b)
circuit board: 8.46667cm x 5.64444cm
breadboards: 1

parts:
  Motor = DC Motor
  Yellow_LED = LED - 5mm [color="Yellow (595nm)" package="5 mm [THT]"]
  Arduino_Nano_V3 = Arduino Nano (Rev3.0)
  R2 = Resistor [tolerance=±1% resistance=330 package=THT]
  Motor_Driver = L293D [package=THT]
  Color_Sensor = TCS34725 RGB Color Sensor
  5V_Power_Jack = 2.1mm Barrel Jack with Terminal Block
  Distance_Sensor = HC-SR04
  R1 = Resistor [tolerance=±1% resistance=330 package=THT]
  U1 = RELAY [package=relay-jzc]
  U2 = RELAY [package=relay-jzc]
  Red_LED = LED - 5mm [color="Red (633nm)" package="5 mm [THT]"]
  Part1 = Bluetooth HC-05 Macho
  S1 = Toggle Switch [package=THT]
  R3 = Resistor [tolerance=±5% resistance=10k package=THT]
  R4 = Resistor [tolerance=±5% resistance=10k package=THT]
  S2 = Toggle Switch [package=THT]

nets:
  N1: Motor.pin_1, Motor_Driver.Out_2_(_Controlled_by_Enable_1_)
  N2: Motor.pin_2, Motor_Driver.Out_1_(_Controlled_by_Enable_1_)
  GND: Yellow_LED.cathode, Arduino_Nano_V3.GND, Arduino_Nano_V3.A2, Motor_Driver.0V, Color_Sensor.GND, 5V_Power_Jack.NEG, Distance_Sensor.Gnd, U1.COIL2, U1.NC, U2.COIL2, Red_LED.cathode, Part1.GND, R3.Pin_1, R4.Pin_1
  N3: Yellow_LED.anode, R1.Pin_1
  N4: Arduino_Nano_V3.RESET, Arduino_Nano_V3.A0, S1.COM, R4.Pin_0
  N5: Arduino_Nano_V3.D2, Part1.RXD
  N6: Arduino_Nano_V3.D3, Part1.TXD
  N7: Arduino_Nano_V3.D4, Color_Sensor.LED
  N8: Arduino_Nano_V3.D5, Motor_Driver.Enable_1
  N9: Arduino_Nano_V3.D6, Motor_Driver.In_2
  N10: Arduino_Nano_V3.D7, Motor_Driver.In_1
  N11: Arduino_Nano_V3.D8, R2.Pin_1
  N12: Arduino_Nano_V3.D9, R1.Pin_0
  N13: Arduino_Nano_V3.D10, R3.Pin_0, S2.COM
  N14: Arduino_Nano_V3.D11/MOSI, Distance_Sensor.Echo
  N15: Arduino_Nano_V3.D12/MISO, Distance_Sensor.Trig
  VCC: Arduino_Nano_V3.VIN, Motor_Driver.+Vmotor, Color_Sensor.VDD, 5V_Power_Jack.POS, Distance_Sensor.Vcc, U1.NO, U2.NO, Part1.VCC, S1.L2, S2.L2
  N16: Arduino_Nano_V3.A5, Color_Sensor.SCL
  N17: Arduino_Nano_V3.A4, Color_Sensor.SDA
  N18: Arduino_Nano_V3.A1, U2.NC
  N19: R2.Pin_0, Red_LED.anode

custom parts:
  TCS34725 RGB Color Sensor: TCS34725 RGB Color Sensor with LED
  HC-SR04: HC-SR04 ultrasonic distance sensor
