# Fritzing sketch button_fritz (saved by Fritzing 0.9.2b)
breadboards: 1

parts:
  Bauteil1 = Arduino Nano (Rev3.0)
  S1 = Pushbutton [package="[SMD]"]
  R1 = Resistor [tolerance=±5% resistance=10k package="2010 [SMD]"]

nets:
  N1: Bauteil1.GND, R1.Pin_0
  N2: Bauteil1.D2, S1.Pin_1, S1.Pin_2
  N3: Bauteil1.5V, S1.Pin_3, S1.Pin_4, R1.Pin_1
