# Fritzing sketch carsim (saved by Fritzing 0.9.2b)
breadboards: 1

parts:
  Part1 = Arduino Nano (Rev3.0)
  Part2 = RFID-RC522-v2
  Part3 = SRF05 Ultrasonic Rangefinder
  S1 = Pushbutton [package="[THT]"]
  R1 = Resistor [tolerance=±5% resistance=10k package="0805 [SMD]"]
  LED1 = LEDs [package=led10mm]
  R2 = Resistor [tolerance=±5% resistance=220 package="0805 [SMD]"]

nets:
  GND: Part1.GND, Part2.GND, Part3.GND, R1.Pin_0, LED1.A
  N1: Part1.D2, S1.Pin_1, S1.Pin_2, R1.Pin_1
  N2: Part1.D3, R2.Pin_0
  N3: Part1.D5, Part3.Echo
  N4: Part1.D6, Part3.Trig
  N5: Part1.D9, Part2.RST
  N6: Part1.D10, Part2.SDA
  N7: Part1.D11/MOSI, Part2.MOSI
  N8: Part1.D12/MISO, Part2.MISO
  5V: Part1.5V, Part3.VCC, S1.Pin_3, S1.Pin_4
  3V3: Part1.3V3, Part2.3.3V
  N9: Part1.D13/SCK, Part2.SCK
  N10: LED1.C, R2.Pin_1

custom parts:
  RFID-RC522-v2: A simple China made RFID-RC522 Reader; do check the pin labels, as this is a MFRC522 based clone.
