# Fritzing sketch carsim_fritz (saved by Fritzing 0.9.2b)
breadboards: 1

parts:
  Bauteil1 = Arduino Nano (Rev3.0)
  Bauteil2 = RFID-RC522-v2
  R1 = Resistor [tolerance=±5% resistance=10k package="2010 [SMD]"]
  S1 = Pushbutton [package="[SMD]"]
  Rot1 = LED - 5mm [color="Red (633nm)" package="5 mm [THT]"]
  R4 = Resistor [tolerance=±5% resistance=220 package=THT]
  Part2 = SRF05 Ultrasonic Rangefinder

nets:
  GND: Bauteil1.GND, Bauteil2.GND, R1.Pin_0, Rot1.anode, Part2.GND
  N1: Bauteil1.D2, R1.Pin_1, S1.Pin_1, S1.Pin_2
  N2: Bauteil1.D3, R4.Pin_0
  N3: Bauteil1.D6, Part2.Trig
  N4: Bauteil1.D8, Part2.Echo
  N5: Bauteil1.D9, Bauteil2.RST
  N6: Bauteil1.D10, Bauteil2.SDA
  N7: Bauteil1.D11/MOSI, Bauteil2.MOSI
  N8: Bauteil1.D12/MISO, Bauteil2.MISO
  5V: Bauteil1.5V, S1.Pin_3, S1.Pin_4, Part2.VCC
  3V3: Bauteil1.3V3, Bauteil2.3.3V
  N9: Bauteil1.D13/SCK, Bauteil2.SCK
  N10: Rot1.cathode, R4.Pin_1

custom parts:
  RFID-RC522-v2: A simple China made RFID-RC522 Reader; do check the pin labels, as this is a MFRC522 based clone.
