# Fritzing sketch LEDSteckplan (saved by Fritzing 0.9.2b)
circuit board: 8.46667cm x 5.64444cm
breadboards: 1

parts:
  Bauteil1 = Arduino Nano (Rev3.0)
  R1 = Resistor [tolerance=±5% resistance=220 package=THT]
  R2 = Resistor [tolerance=±5% resistance=220 package=THT]
  R3 = Resistor [tolerance=±5% resistance=220 package=THT]
  Rot = LED - 5mm [color="Red (633nm)" package="5 mm [THT]"]
  Gelb = LED - 5mm [color="Yellow (585nm)" package="5 mm [THT]"]
  Grün = LED - 5mm [color="Green (565nm)" package="5 mm [THT]"]

nets (from the schematic view):
  N1: Bauteil1.GND, Rot.cathode, Gelb.cathode, Gelb.anode, Grün.cathode
  N2: Bauteil1.D10, R1.Pin_0
  N3: Bauteil1.D11/MOSI, R2.Pin_0
  N4: Bauteil1.D12/MISO, R3.Pin_0
  N5: R1.Pin_1, Grün.anode
  N6: R3.Pin_1, Rot.anode

// code stored in the sketch: Ampel (fritzing).ino

