# Fritzing sketch pingecho (saved by Fritzing 0.9.2b)
breadboards: 1

parts:
  Part1 = SRF05 Ultrasonic Rangefinder
  Part2 = Arduino Ethernet Shield (Rev3)

nets:
  VCC: Part1.VCC, Part2.5V
  N1: Part1.Trig, Part2.ETH_CS
  N2: Part1.Echo, Part2.D8
  GND: Part1.GND, Part2.GND
