# Fritzing sketch rfid_fritz (saved by Fritzing 0.9.2b)
breadboards: 1

parts:
  Bauteil1 = Arduino Nano (Rev3.0)
  Bauteil2 = RFID-RC522-v2

nets:
  GND: Bauteil1.GND, Bauteil2.GND
  N1: Bauteil1.D9, Bauteil2.RST
  N2: Bauteil1.D10, Bauteil2.SDA
  N3: Bauteil1.D11/MOSI, Bauteil2.MOSI
  N4: Bauteil1.D12/MISO, Bauteil2.MISO
  3V3: Bauteil1.3V3, Bauteil2.3.3V
  N5: Bauteil1.D13/SCK, Bauteil2.SCK

custom parts:
  RFID-RC522-v2: A simple China made RFID-RC522 Reader; do check the pin labels, as this is a MFRC522 based clone.
